// Logisim project lab3-emma.circ as structural Verilog
module half_adder (
  input  A,
  input  B,
  output Sum,
  output Cout
);

  xor xor_1 (Sum, A, B);
  and and_1 (Cout, A, B);
endmodule

module full_adder (
  input  A,
  input  B,
  input  Cin,
  output Sum,
  output Cout
);

  wire half_adder_2_cout, half_adder_cout, half_adder_sum;

  half_adder half_adder (.A(A), .B(B), .Sum(half_adder_sum), .Cout(half_adder_cout));
  half_adder half_adder_2 (.A(half_adder_sum), .B(Cin), .Sum(Sum), .Cout(half_adder_2_cout));
  or or_1 (Cout, half_adder_2_cout, half_adder_cout);
endmodule

module _2_mux (
  input  A,
  input  B,
  input  Sel,
  output \output 
);

  wire and_1_out, and_2_out, not_1_out;

  and and_1 (and_1_out, A, not_1_out);
  not not_1 (not_1_out, Sel);
  and and_2 (and_2_out, B, Sel);
  or or_1 (\output , and_1_out, and_2_out);
endmodule

module _4_mux (
  input  A,
  input  B,
  input  C,
  input  D,
  input  Sel_1,
  input  Sel_0,
  output \output 
);

  wire _2_mux_2_output, _2_mux_output;

  _2_mux _2_mux (.A(A), .B(B), .Sel(Sel_0), .\output (_2_mux_output));
  _2_mux _2_mux_2 (.A(C), .B(D), .Sel(Sel_0), .\output (_2_mux_2_output));
  _2_mux _2_mux_3 (.A(_2_mux_output), .B(_2_mux_2_output), .Sel(Sel_1), .\output (\output ));
endmodule

module _1_bit_alu (
  input  A,
  input  B,
  input  Cin,
  input  Sel_1,
  input  Sel_0,
  output Cout,
  output out_7
);

  wire and_1_out, full_adder_sum, or_1_out;

  Full_Adder full_adder (.A(A), .B(B), .Cin(Cin), .Sum(full_adder_sum), .Cout(Cout));
  and and_1 (and_1_out, A, B);
  or or_1 (or_1_out, A, B);
  _4_mux _4_mux (
    .A(full_adder_sum), .B(and_1_out), .C(or_1_out), .Sel_1(Sel_1), .Sel_0(Sel_0), .\output (out_7));  // open: D

  // Notes on the sheet:
  //   Sum
endmodule

module xor_gate (
  input  A,
  input  B,
  output out_3
);

  wire and_1_out, and_2_out, not_1_out, not_2_out;

  not not_1 (not_1_out, A);
  and and_1 (and_1_out, not_1_out, B);
  and and_2 (and_2_out, A, not_2_out);
  not not_2 (not_2_out, B);
  or or_1 (out_3, and_1_out, and_2_out);
endmodule

module Full_Adder (
  input  A,
  input  B,
  input  Cin,
  output Sum,
  output Cout
);

  wire half_adder_2_cout, half_adder_cout, half_adder_sum;

  Half_Adder half_adder (.A(A), .B(B), .Sum(half_adder_sum), .Cout(half_adder_cout));
  Half_Adder half_adder_2 (.A(half_adder_sum), .B(Cin), .Sum(Sum), .Cout(half_adder_2_cout));
  or or_1 (Cout, half_adder_2_cout, half_adder_cout);

  // Notes on the sheet:
  //   Sum
  //   Cout
endmodule

module Half_Adder (
  input  A,
  input  B,
  output Sum,
  output Cout
);

  xor_gate \xor  (.A(A), .B(B), .out_3(Sum));
  and and_1 (Cout, A, B);
endmodule

module _4_bit_ripple (
  input  A3,
  input  B3,
  input  B2,
  input  A1,
  input  B1,
  input  A0,
  input  B0,
  input  Sel_1,
  input  Sel_0,
  input  A2,
  output Cout,
  output Sum,
  output Sum_2,
  output Sum_3,
  output Sum_4
);

  wire _1_bit_ALU_2_cout, _1_bit_ALU_3_cout, _1_bit_ALU_4_cout, and_1_out;

  _1_bit_alu _1_bit_ALU (
    .Cout(Cout), .Sel_1(Sel_1), .Sel_0(Sel_0), .A(A3), .B(B3), .Cin(_1_bit_ALU_2_cout), .out_7(Sum));
  _1_bit_alu _1_bit_ALU_2 (
    .Cout(_1_bit_ALU_2_cout), .Sel_1(Sel_1), .Sel_0(Sel_0), .A(A2), .B(B2), .Cin(_1_bit_ALU_3_cout),
    .out_7(Sum_4));
  _1_bit_alu _1_bit_ALU_3 (
    .Cout(_1_bit_ALU_3_cout), .Sel_1(Sel_1), .Sel_0(Sel_0), .A(A1), .B(B1), .Cin(_1_bit_ALU_4_cout),
    .out_7(Sum_2));
  _1_bit_alu _1_bit_ALU_4 (
    .Cout(_1_bit_ALU_4_cout), .Sel_1(Sel_1), .Sel_0(Sel_0), .A(A0), .B(B0), .Cin(and_1_out), .out_7(Sum_3));
  and and_1 (and_1_out, Sel_1, Sel_0);
endmodule

module Full_4_bit_alu (
  input  A3,
  input  B3,
  input  B2,
  input  A1,
  input  B1,
  input  A0,
  input  B0,
  input  Sel_1,
  input  Sel_0,
  input  A2,
  output Cout,
  output Sum,
  output Sum_2,
  output Sum_3,
  output Sum_4
);

  wire and_1_out, Full_1_bit_ALU_2_cout, Full_1_bit_ALU_3_cout, Full_1_bit_ALU_4_cout;

  Full_1_bit_alu Full_1_bit_ALU (
    .Cout(Cout), .Sel_1(Sel_1), .Sel_0(Sel_0), .A(A3), .B(B3), .out_7(Sum_2), .Cin(Full_1_bit_ALU_2_cout));
  Full_1_bit_alu Full_1_bit_ALU_2 (
    .Cout(Full_1_bit_ALU_2_cout), .Sel_1(Sel_1), .Sel_0(Sel_0), .A(A2), .B(B2), .out_7(Sum),
    .Cin(Full_1_bit_ALU_3_cout));
  Full_1_bit_alu Full_1_bit_ALU_3 (
    .Cout(Full_1_bit_ALU_3_cout), .Sel_1(Sel_1), .Sel_0(Sel_0), .A(A1), .B(B1), .out_7(Sum_3),
    .Cin(Full_1_bit_ALU_4_cout));
  Full_1_bit_alu Full_1_bit_ALU_4 (
    .Cout(Full_1_bit_ALU_4_cout), .Sel_1(Sel_1), .Sel_0(Sel_0), .A(A0), .B(B0), .out_7(Sum_4), .Cin(and_1_out));
  and and_1 (and_1_out, Sel_1, Sel_0);
endmodule

module Full_1_bit_alu (
  input  A,
  input  B,
  input  Cin,
  input  Sel_1,
  input  Sel_0,
  output Cout,
  output out_7
);

  wire _2_mux_output, and_1_out, and_2_out, Full_Adder_sum, not_1_out, or_1_out;

  and and_1 (and_1_out, Sel_1, Sel_0);
  not not_1 (not_1_out, B);
  _2_mux _2_mux (.A(B), .B(not_1_out), .Sel(and_1_out), .\output (_2_mux_output));
  Full_Adder Full_Adder (.A(A), .B(_2_mux_output), .Cin(Cin), .Sum(Full_Adder_sum), .Cout(Cout));
  and and_2 (and_2_out, A, B);
  _4_mux _4_mux (
    .A(Full_Adder_sum), .B(and_2_out), .C(or_1_out), .D(Full_Adder_sum), .Sel_1(Sel_1), .Sel_0(Sel_0),
    .\output (out_7));
  or or_1 (or_1_out, A, B);

  // Notes on the sheet:
  //   Sum
endmodule

module register_file (
  input  [3:0] Data_In,
  input  WE,
  input  [2:0] RA1,
  input  [2:0] WA,
  input  [2:0] RA2,
  input  CLK,
  output [3:0] Data_1_Out,
  output [3:0] Data_2_Out
);

  wire demultiplexer_1_out0, demultiplexer_1_out1, demultiplexer_1_out2, demultiplexer_1_out3,
       demultiplexer_1_out4, demultiplexer_1_out5, demultiplexer_1_out6, demultiplexer_1_out7;
  wire [3:0] _4_bit_register_2_data_out, _4_bit_register_3_data_out, _4_bit_register_4_data_out,
       _4_bit_register_5_data_out, _4_bit_register_6_data_out, _4_bit_register_7_data_out,
       _4_bit_register_8_data_out, _4_bit_register_data_out;

  Demultiplexer #(.select(3)) demultiplexer_1 (
    .out0(demultiplexer_1_out0), .out1(demultiplexer_1_out1), .out2(demultiplexer_1_out2),
    .out3(demultiplexer_1_out3), .out4(demultiplexer_1_out4), .out5(demultiplexer_1_out5),
    .out6(demultiplexer_1_out6), .out7(demultiplexer_1_out7), .in(WE), .sel(WA));  // open: en
  _4_bit_register _4_bit_register (
    .Data_In(Data_In), .E(demultiplexer_1_out0), .CLK(CLK), .Data_Out(_4_bit_register_data_out));
  _4_bit_register _4_bit_register_2 (
    .Data_In(Data_In), .E(demultiplexer_1_out1), .CLK(CLK), .Data_Out(_4_bit_register_2_data_out));
  _4_bit_register _4_bit_register_3 (
    .Data_In(Data_In), .E(demultiplexer_1_out2), .CLK(CLK), .Data_Out(_4_bit_register_3_data_out));
  _4_bit_register _4_bit_register_4 (
    .Data_In(Data_In), .E(demultiplexer_1_out3), .CLK(CLK), .Data_Out(_4_bit_register_4_data_out));
  _4_bit_register _4_bit_register_5 (
    .Data_In(Data_In), .E(demultiplexer_1_out4), .CLK(CLK), .Data_Out(_4_bit_register_5_data_out));
  _4_bit_register _4_bit_register_6 (
    .Data_In(Data_In), .E(demultiplexer_1_out5), .CLK(CLK), .Data_Out(_4_bit_register_6_data_out));
  _4_bit_register _4_bit_register_7 (
    .Data_In(Data_In), .E(demultiplexer_1_out6), .CLK(CLK), .Data_Out(_4_bit_register_7_data_out));
  _4_bit_register _4_bit_register_8 (
    .Data_In(Data_In), .E(demultiplexer_1_out7), .CLK(CLK), .Data_Out(_4_bit_register_8_data_out));
  // Probe on _4_bit_register_data_out
  // Probe on _4_bit_register_2_data_out
  // Probe on _4_bit_register_8_data_out
  Multiplexer #(.select(3), .width(4)) multiplexer_1 (
    .in0(_4_bit_register_data_out), .in1(_4_bit_register_2_data_out), .in2(_4_bit_register_3_data_out),
    .in3(_4_bit_register_4_data_out), .in4(_4_bit_register_5_data_out), .in5(_4_bit_register_6_data_out),
    .in6(_4_bit_register_7_data_out), .in7(_4_bit_register_8_data_out), .out(Data_1_Out), .sel(RA1));  // open: en
  Multiplexer #(.select(3), .width(4)) multiplexer_2 (
    .in0(_4_bit_register_data_out), .in1(_4_bit_register_2_data_out), .in2(_4_bit_register_3_data_out),
    .in3(_4_bit_register_4_data_out), .in4(_4_bit_register_5_data_out), .in5(_4_bit_register_6_data_out),
    .in6(_4_bit_register_7_data_out), .in7(_4_bit_register_8_data_out), .out(Data_2_Out), .sel(RA2));  // open: en
endmodule

module _4_bit_register (
  input  [3:0] Data_In,
  input  E,
  input  CLK,
  output [3:0] Data_Out
);

  D_Flip_Flop d_ff_1 (.clk(CLK), .D(Data_In[0]), .Q(Data_Out[0]), .en(E));  // open: Qn, preset, reset
  D_Flip_Flop d_ff_2 (.clk(CLK), .D(Data_In[1]), .Q(Data_Out[1]), .en(E));  // open: Qn, preset, reset
  D_Flip_Flop d_ff_3 (.clk(CLK), .D(Data_In[2]), .Q(Data_Out[2]), .en(E));  // open: Qn, preset, reset
  D_Flip_Flop d_ff_4 (.clk(CLK), .D(Data_In[3]), .Q(Data_Out[3]), .en(E));  // open: Qn, preset, reset
endmodule

module data_path (
  input  WE,
  input  CLK,
  input  [11:0] Instruction_Word
);

  wire [3:0] _4_bit_2_mux_output, bit_extender_1_out, full_4_bit_alu_sum_4, register_file_data_1_out,
       register_file_data_2_out;

  register_file register_file (
    .Data_In(full_4_bit_alu_sum_4), .WE(WE), .CLK(CLK), .WA(Instruction_Word[8:6]),
    .RA1(Instruction_Word[5:3]), .RA2(Instruction_Word[2:0]), .Data_1_Out(register_file_data_1_out),
    .Data_2_Out(register_file_data_2_out));
  assign bit_extender_1_out = {{1{Instruction_Word[2]}}, Instruction_Word[2:0]};  // Bit_Extender bit_extender_1
  _4_bit_2_mux _4_bit_2_mux (
    .A0(register_file_data_2_out[0]), .B0(bit_extender_1_out[0]), .A1(register_file_data_2_out[1]),
    .B1(bit_extender_1_out[1]), .A2(register_file_data_2_out[2]), .B2(bit_extender_1_out[2]),
    .A3(register_file_data_2_out[3]), .B3(bit_extender_1_out[3]), .S(Instruction_Word[11]),
    .Output(_4_bit_2_mux_output));
  Full_4_bit_alu full_4_bit_alu (
    .Cout(full_4_bit_alu_sum_4[3]), .A3(register_file_data_1_out[3]), .B3(_4_bit_2_mux_output[3]),
    .A2(register_file_data_1_out[2]), .B2(_4_bit_2_mux_output[2]), .A1(register_file_data_1_out[1]),
    .B1(_4_bit_2_mux_output[1]), .A0(register_file_data_1_out[0]), .B0(_4_bit_2_mux_output[0]),
    .Sel_1(Instruction_Word[10]), .Sel_0(Instruction_Word[9]), .Sum(full_4_bit_alu_sum_4[2]),
    .Sum_3(full_4_bit_alu_sum_4[1]), .Sum_4(full_4_bit_alu_sum_4[0]));  // open: Sum_2
endmodule

module _4_bit_2_mux (
  input  A0,
  input  B0,
  input  A1,
  input  B1,
  input  A2,
  input  B2,
  input  A3,
  input  B3,
  input  S,
  output [3:0] Output
);

  _2_mux _2_mux (.A(A0), .B(B0), .Sel(S), .\output (Output[0]));
  _2_mux _2_mux_2 (.A(A1), .B(B1), .Sel(S), .\output (Output[1]));
  _2_mux _2_mux_3 (.A(A2), .B(B2), .Sel(S), .\output (Output[2]));
  _2_mux _2_mux_4 (.A(A3), .B(B3), .Sel(S), .\output (Output[3]));
endmodule
