// Logisim project lab2-emma.circ as structural Verilog
module half_adder (
  input  A,
  input  B,
  output Sum,
  output Cout
);

  xor xor_1 (Sum, A, B);
  and and_1 (Cout, A, B);
endmodule

module full_adder (
  input  A,
  input  B,
  input  Cin,
  output Sum,
  output Cout
);

  wire half_adder_2_cout, half_adder_cout, half_adder_sum;

  half_adder half_adder (.A(A), .B(B), .Sum(half_adder_sum), .Cout(half_adder_cout));
  half_adder half_adder_2 (.A(half_adder_sum), .B(Cin), .Sum(Sum), .Cout(half_adder_2_cout));
  or or_1 (Cout, half_adder_2_cout, half_adder_cout);
endmodule

module _2_mux (
  input  A,
  input  B,
  input  Sel,
  output \output 
);

  wire and_1_out, and_2_out, not_1_out;

  and and_1 (and_1_out, A, not_1_out);
  not not_1 (not_1_out, Sel);
  and and_2 (and_2_out, B, Sel);
  or or_1 (\output , and_1_out, and_2_out);
endmodule

module _4_mux (
  input  A,
  input  B,
  input  C,
  input  D,
  input  Sel_1,
  input  Sel_0,
  output \output 
);

  wire _2_mux_2_output, _2_mux_output;

  _2_mux _2_mux (.A(A), .B(B), .Sel(Sel_0), .\output (_2_mux_output));
  _2_mux _2_mux_2 (.A(C), .B(D), .Sel(Sel_0), .\output (_2_mux_2_output));
  _2_mux _2_mux_3 (.A(_2_mux_output), .B(_2_mux_2_output), .Sel(Sel_1), .\output (\output ));
endmodule

module _1_bit_alu (
  input  A,
  input  B,
  input  Cin,
  input  Sel_1,
  input  Sel_0,
  output Cout,
  output out_7
);

  wire and_1_out, full_adder_sum, or_1_out;

  Full_Adder full_adder (.A(A), .B(B), .Cin(Cin), .Sum(full_adder_sum), .Cout(Cout));
  and and_1 (and_1_out, A, B);
  or or_1 (or_1_out, A, B);
  _4_mux _4_mux (
    .A(full_adder_sum), .B(and_1_out), .C(or_1_out), .Sel_1(Sel_1), .Sel_0(Sel_0), .\output (out_7));  // open: D

  // Notes on the sheet:
  //   Sum
endmodule

module xor_gate (
  input  A,
  input  B,
  output out_3
);

  wire and_1_out, and_2_out, not_1_out, not_2_out;

  not not_1 (not_1_out, A);
  and and_1 (and_1_out, not_1_out, B);
  and and_2 (and_2_out, A, not_2_out);
  not not_2 (not_2_out, B);
  or or_1 (out_3, and_1_out, and_2_out);
endmodule

module Full_Adder (
  input  A,
  input  B,
  input  Cin,
  output Sum,
  output Cout
);

  wire half_adder_2_cout, half_adder_cout, half_adder_sum;

  Half_Adder half_adder (.A(A), .B(B), .Sum(half_adder_sum), .Cout(half_adder_cout));
  Half_Adder half_adder_2 (.A(half_adder_sum), .B(Cin), .Sum(Sum), .Cout(half_adder_2_cout));
  or or_1 (Cout, half_adder_2_cout, half_adder_cout);

  // Notes on the sheet:
  //   Sum
  //   Cout
endmodule

module Half_Adder (
  input  A,
  input  B,
  output Sum,
  output Cout
);

  xor_gate \xor  (.A(A), .B(B), .out_3(Sum));
  and and_1 (Cout, A, B);
endmodule

module _4_bit_ripple (
  input  A3,
  input  B3,
  input  B2,
  input  A1,
  input  B1,
  input  A0,
  input  B0,
  input  Sel_1,
  input  Sel_0,
  input  A2,
  output Cout,
  output Sum,
  output Sum_2,
  output Sum_3,
  output Sum_4
);

  wire _1_bit_ALU_2_cout, _1_bit_ALU_3_cout, _1_bit_ALU_4_cout, and_1_out;

  _1_bit_alu _1_bit_ALU (
    .Cout(Cout), .Sel_1(Sel_1), .Sel_0(Sel_0), .A(A3), .B(B3), .Cin(_1_bit_ALU_2_cout), .out_7(Sum));
  _1_bit_alu _1_bit_ALU_2 (
    .Cout(_1_bit_ALU_2_cout), .Sel_1(Sel_1), .Sel_0(Sel_0), .A(A2), .B(B2), .Cin(_1_bit_ALU_3_cout),
    .out_7(Sum_4));
  _1_bit_alu _1_bit_ALU_3 (
    .Cout(_1_bit_ALU_3_cout), .Sel_1(Sel_1), .Sel_0(Sel_0), .A(A1), .B(B1), .Cin(_1_bit_ALU_4_cout),
    .out_7(Sum_2));
  _1_bit_alu _1_bit_ALU_4 (
    .Cout(_1_bit_ALU_4_cout), .Sel_1(Sel_1), .Sel_0(Sel_0), .A(A0), .B(B0), .Cin(and_1_out), .out_7(Sum_3));
  and and_1 (and_1_out, Sel_1, Sel_0);
endmodule

module Full_4_bit_alu (
  input  A3,
  input  B3,
  input  B2,
  input  A1,
  input  B1,
  input  A0,
  input  B0,
  input  Sel_1,
  input  Sel_0,
  input  A2,
  output Cout,
  output Sum,
  output Sum_2,
  output Sum_3,
  output Sum_4
);

  wire and_1_out, Full_1_bit_ALU_2_cout, Full_1_bit_ALU_3_cout, Full_1_bit_ALU_4_cout;

  Full_1_bit_alu Full_1_bit_ALU (
    .Cout(Cout), .Sel_1(Sel_1), .Sel_0(Sel_0), .A(A3), .B(B3), .out_7(Sum_2), .Cin(Full_1_bit_ALU_2_cout));
  Full_1_bit_alu Full_1_bit_ALU_2 (
    .Cout(Full_1_bit_ALU_2_cout), .Sel_1(Sel_1), .Sel_0(Sel_0), .A(A2), .B(B2), .out_7(Sum),
    .Cin(Full_1_bit_ALU_3_cout));
  Full_1_bit_alu Full_1_bit_ALU_3 (
    .Cout(Full_1_bit_ALU_3_cout), .Sel_1(Sel_1), .Sel_0(Sel_0), .A(A1), .B(B1), .out_7(Sum_3),
    .Cin(Full_1_bit_ALU_4_cout));
  Full_1_bit_alu Full_1_bit_ALU_4 (
    .Cout(Full_1_bit_ALU_4_cout), .Sel_1(Sel_1), .Sel_0(Sel_0), .A(A0), .B(B0), .out_7(Sum_4), .Cin(and_1_out));
  and and_1 (and_1_out, Sel_1, Sel_0);
endmodule

module Full_1_bit_alu (
  input  A,
  input  B,
  input  Cin,
  input  Sel_1,
  input  Sel_0,
  output Cout,
  output out_7
);

  wire _2_mux_output, and_1_out, and_2_out, Full_Adder_sum, not_1_out, or_1_out;

  and and_1 (and_1_out, Sel_1, Sel_0);
  not not_1 (not_1_out, B);
  _2_mux _2_mux (.A(B), .B(not_1_out), .Sel(and_1_out), .\output (_2_mux_output));
  Full_Adder Full_Adder (.A(A), .B(_2_mux_output), .Cin(Cin), .Sum(Full_Adder_sum), .Cout(Cout));
  and and_2 (and_2_out, A, B);
  _4_mux _4_mux (
    .A(Full_Adder_sum), .B(and_2_out), .C(or_1_out), .D(Full_Adder_sum), .Sel_1(Sel_1), .Sel_0(Sel_0),
    .\output (out_7));
  or or_1 (or_1_out, A, B);

  // Notes on the sheet:
  //   Sum
endmodule
